# Fritzing sketch 07a-us-sensing-intro (saved by Fritzing 1.0.4)
breadboards: 1

parts:
  R1 = Resistor [tolerance=±5% power=0.25W resistance=330 package=THT]
  R2 = Resistor [tolerance=±5% power=0.25W resistance=470 package=THT]
  HC-SR04_Sensor_1 = HC-SR04 Ultrasonic Distance Sensor
  Mod1 = Raspberry Pi 4B

nets:
  N1: R1.Pin_0, R2.Pin_1, Mod1.GPIO24
  N2: R1.Pin_1, HC-SR04_Sensor_1.ECHO
  GND: R2.Pin_0, HC-SR04_Sensor_1.GND, Mod1.GND
  VCC: HC-SR04_Sensor_1.VCC, Mod1.5V
  N3: HC-SR04_Sensor_1.TRIG, Mod1.GPIO18
