# Fritzing sketch 08a-servo-motors-intro (saved by Fritzing 1.0.4)

parts:
  M1 = Dagu DGServo 9g (Top view) [part_number=RS001B]
  Mod1 = Raspberry Pi 4B

nets:
  GND: M1.gnd, Mod1.GND
  VCC: M1.vcc, Mod1.5V
  N1: M1.pulse, Mod1.GPIO17
