# Fritzing sketch 09b-keypad-piezo (saved by Fritzing 1.0.4)

parts:
  Matrix_keypad1 = KEYPAD 4x4
  Mod1 = Raspberry Pi 4B
  J1 = Piezo Speaker

nets:
  N1: Matrix_keypad1.col1, Mod1.GPIO24
  N2: Matrix_keypad1.col2, Mod1.GPIO25
  N3: Matrix_keypad1.col3, Mod1.GPIO8
  N4: Matrix_keypad1.col4, Mod1.GPIO7
  N5: Matrix_keypad1.row1, Mod1.GPIO12
  N6: Matrix_keypad1.row2, Mod1.GPIO16
  N7: Matrix_keypad1.row3, Mod1.GPIO20
  N8: Matrix_keypad1.row4, Mod1.GPIO21
  N9: Mod1.GND, J1.pin1
  N10: Mod1.GPIO18, J1.pin2

custom parts:
  KEYPAD 4x4: Matrix keypad 16 buttons, 4 rows x 4 columns
