# Fritzing sketch 09c-keypad-piezo-buzzer-us (saved by Fritzing 1.0.4)
breadboards: 1

parts:
  Matrix_keypad1 = KEYPAD 4x4
  Mod1 = Raspberry Pi 4B
  J1 = Piezo Speaker
  HC-SR04_Sensor_1 = HC-SR04 Ultrasonic Distance Sensor
  R1 = Resistor [tolerance=±5% resistance=220 package="2010 [SMD]"]
  R2 = Resistor [tolerance=±5% resistance=47 package="2010 [SMD]"]

nets:
  N1: Matrix_keypad1.col1, Mod1.GPIO24
  N2: Matrix_keypad1.col2, Mod1.GPIO25
  N3: Matrix_keypad1.col3, Mod1.GPIO8
  N4: Matrix_keypad1.col4, Mod1.GPIO7
  N5: Matrix_keypad1.row1, Mod1.GPIO12
  N6: Matrix_keypad1.row2, Mod1.GPIO16
  N7: Matrix_keypad1.row3, Mod1.GPIO20
  N8: Matrix_keypad1.row4, Mod1.GPIO21
  5V: Mod1.5V, HC-SR04_Sensor_1.VCC
  GND: Mod1.GND, J1.pin1, HC-SR04_Sensor_1.GND, R2.Pin_1
  N9: Mod1.GPIO18, J1.pin2
  N10: Mod1.GPIO5, R1.Pin_1, R2.Pin_0
  N11: Mod1.GPIO6, HC-SR04_Sensor_1.TRIG
  N12: HC-SR04_Sensor_1.ECHO, R1.Pin_0

custom parts:
  KEYPAD 4x4: Matrix keypad 16 buttons, 4 rows x 4 columns
