# Fritzing sketch reaction-circuit (saved by Fritzing 1.0.2b)
breadboards: 1

parts:
  Mod1 = Raspberry Pi 4B
  S1 = Pushbutton [package="[THT]"]
  S2 = Pushbutton [package="[THT]"]
  LED1 = LED - 3mm [color="Red (633nm)" current=0.030A package="3 mm [THT]"]
  R1 = Resistor [tolerance=±5% resistance=220 package="2512 [SMD]"]

nets:
  N1: Mod1.3V3, S1.Pin_3, S1.Pin_4, S2.Pin_3, S2.Pin_4
  N2: Mod1.GND, R1.Pin_1
  N3: Mod1.GPIO17, S1.Pin_1, S1.Pin_2
  N4: Mod1.GPIO27, S2.Pin_1, S2.Pin_2
  N5: Mod1.GPIO22, LED1.anode
  N6: LED1.cathode, R1.Pin_0
